# Fritzing sketch hifi-remote (saved by Fritzing 0.9.3b)

parts:
  Part1 = Arduino Pro Mini v13
  D1 = LTE-302 [package=lte-302]
  IR1 = TSOP312.., 314.. [package=THT]
  U3 = mystery part, 3 pins [chip_label=?]
  R1 = Resistor [tolerance=±5% resistance=220 package="0402 [SMD]"]
  R2 = Resistor [tolerance=±5% resistance=2.2k package=THT]
  Q1 = TIP120 Hi-Current Darlington Transistor
  U4 = Mini-360 DC-DC Buck converter [package=THT]

nets:
  N1: Part1.VCC, IR1.Vs, U3.pin3, U4.IN+
  GND: Part1.GND, D1.C, IR1.GND, U3.pin2, Q1.EMITTER
  N2: Part1.D11_PWM/MOSI, IR1.Data
  N3: Part1.D9_PWM, R2.Pin_0
  N4: Part1.D3_PWM, R1.Pin_1
  N5: Part1.D2, U3.pin1
  N6: D1.A, R1.Pin_0
  N7: R2.Pin_1, Q1.BASE
  N8: Q1.COLLECTOR, U4.IN-

notes:
  433mhz receiver
  Power for Bluetooth Dongle (9v)

custom parts:
  Mini-360 DC-DC Buck converter: Mini-360 DC-DC Buck converter. Tiny buck step down voltage converter, input voltage 4.75 to 23V output 1 to 17V adjustable. Available from ebay and the like.
